# Fritzing sketch dht-iot (saved by Fritzing 0.9.4)

parts:
  Part1 = LCD1602-I2C
  A1 = DORHEA ESP32 GPIO breakout board 30pin
  M1 = DOIT Esp32 DevKit v1 (30 pins long, 11 pins width) [part_number=ESP32S-PIN30]  # not connected
  J1 = DHT11 basic temperature-humidity sensor [form="♂ (male)" package=THT]
  JACK1 = 2.1mm Barrel Jack with Terminal Block
  U1 = LIPO-2000mAh [package=lipo-2000]

nets:
  GND: Part1.GND, A1.Pin_67, A1.Pin_85, A1.Pin_96, A1.Pin_101, J1.GND
  N1: Part1.VCC, A1.Pin_86
  N2: Part1.SDA, A1.Pin_87, A1.Pin_123
  N3: Part1.SCL, A1.Pin_88, A1.Pin_126
  N4: A1.Pin_64, A1.Pin_109, J1.VCC
  N5: A1.Pin_75, A1.Pin_122, J1.OUT
  N6: JACK1.POS, U1.+
  N7: JACK1.NEG, U1.-

custom parts:
  LCD1602-I2C: A standard character display, usually with 2x16 characters. Comes in many colors with LCM1602 IIC attached.
  DORHEA ESP32 GPIO breakout board 30pin: ESP32 shield 30P expansion board, supports two power supply : DC 6.5-16v and USB 5.V
  DOIT Esp32 DevKit v1 (30 pins long, 11 pins width): The DOIT Esp32 DevKit v1 is one of the development board created by DOIT to evaluate the ESP-WROOM-32 module. It is based on the ESP32 microcontroller that boasts Wifi, Bluetooth, Ethernet and Low Power support all in a single chip. (vanepp) made breadboard work, adjusted pin numbering and labels and reduced size of schematic and cleaned up pcb. This chip is 30pins long (2 x15) and 11 pins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
  DHT11 basic temperature-humidity sensor: The DHT11 is a basic, ultra low-cost digital temperature and humidity sensor. It uses a capacitive humidity sensor and a thermistor to measure the surrounding air, and spits out a digital signal on the data pin (no analog input pins needed). Its fairly simple to use, but requires careful timing to grab data. The only real downside of this sensor is you can only get new data from it once every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
